// Logisim project SAP1.circ as structural Verilog: 17 circuits, main circuit RingCounter
module main (
  input  in_1,
  input  in_2
);

  wire button_1_out, button_2_out, button_3_out, CLR, controlpanel_1_auto, controlpanel_1_manual,
       controlpanel_1_program, controlpanel_1_run, CP, EP, nCE, nCLK, nHLT, nLO, nW, T1, T2, T3, T4, T5, T6;
  wire [0:0] BR_CABLE, CS_CABLE;
  wire [1:0] ALU_CABLE;
  wire [2:0] AR_CABLE;
  wire [3:0] dipswitch_1_sw4, instructionregister_1_hn0, IR_CABLE, memoryaddressregister_1_do;
  wire [6:0] MAR_CABLE;
  wire [7:0] aregister_1_do1, bregister_1_out_4, dipswitch_2_sw8, outputregister_1_out_4, PD,
       programcounter_1_out_5, wbus_1_o;

  ControlPanel controlpanel_1 (
    .S2(in_2), .S4(button_1_out), .nHLT(nHLT), .S1(dipswitch_1_sw4), .S3(dipswitch_2_sw8), .CS(button_3_out),
    .SS(button_2_out), .MAN(in_1), .Run(controlpanel_1_run), .Program(controlpanel_1_program),
    .nPS(MAR_CABLE[6]), .PA(MAR_CABLE[4:1]), .PD(PD), .nW(nW), .nCLR(CS_CABLE[0]), .CLR(CLR),
    .CLK(AR_CABLE[2]), .nCLK(nCLK), .MANUAL(controlpanel_1_manual), .AUTO(controlpanel_1_auto));
  DipSwitch #(.number(4)) dipswitch_1 (
    .sw1(dipswitch_1_sw4[3]), .sw2(dipswitch_1_sw4[2]), .sw3(dipswitch_1_sw4[1]), .sw4(dipswitch_1_sw4[0]));
  DipSwitch dipswitch_2 (
    .sw1(dipswitch_2_sw8[7]), .sw2(dipswitch_2_sw8[6]), .sw3(dipswitch_2_sw8[5]), .sw4(dipswitch_2_sw8[4]),
    .sw5(dipswitch_2_sw8[3]), .sw6(dipswitch_2_sw8[2]), .sw7(dipswitch_2_sw8[1]), .sw8(dipswitch_2_sw8[0]));
  Button #(.press("passive")) button_1 (.out(button_1_out));
  Button button_2 (.out(button_2_out));
  LED led_1 (.in(controlpanel_1_manual));
  Button button_3 (.out(button_3_out));
  LED led_2 (.in(controlpanel_1_auto));
  LED led_3 (.in(controlpanel_1_run));
  LED led_4 (.in(controlpanel_1_program));
  // Probe on {CP, EP, MAR_CABLE[0], nCE, IR_CABLE[0], IR_CABLE[3], AR_CABLE[0], AR_CABLE[1], ALU_CABLE[0], ALU_CABLE[1], BR_CABLE[0], nLO}
  // Probe on memoryaddressregister_1_do
  // Probe on instructionregister_1_hn0
  ControllerSequencer controllersequencer_1 (
    .A(instructionregister_1_hn0), .CLK(AR_CABLE[2]), .nCLR(CS_CABLE[0]), .nHLT(nHLT),
    .out_6({CP, EP, MAR_CABLE[0], nCE, IR_CABLE[0], IR_CABLE[3], AR_CABLE[0], AR_CABLE[1], ALU_CABLE[0], ALU_CABLE[1], BR_CABLE[0], nLO}),
    .T({T6, T5, T4, T3, T2, T1}));
  ProgramCounter programcounter_1 (.CP(CP), .nCLK(nCLK), .nCLR(CS_CABLE[0]), .EP(EP), .out_5(programcounter_1_out_5));
  MemoryAddressRegister memoryaddressregister_1 (
    .CLK(AR_CABLE[2]), .nLM(MAR_CABLE[0]), .nPS(MAR_CABLE[6]), .PA(MAR_CABLE[4:1]),
    .DI(programcounter_1_out_5), .DO(memoryaddressregister_1_do));
  ReadAccessMemory readaccessmemory_1 (
    .nCE(nCE), .nW(nW), .ADDR(memoryaddressregister_1_do), .DI(PD), .DO(programcounter_1_out_5));
  InstructionRegister instructionregister_1 (
    .CLK(AR_CABLE[2]), .CLR(CLR), .nLI(IR_CABLE[0]), .nEI(IR_CABLE[3]), .DW(programcounter_1_out_5),
    .HN0(instructionregister_1_hn0), .LNO(programcounter_1_out_5));
  // Probe on wbus_1_o
  WBus wbus_1 (.I(programcounter_1_out_5), .O(wbus_1_o));
  ARegister aregister_1 (
    .CLK(AR_CABLE[2]), .nLA(AR_CABLE[0]), .EA(AR_CABLE[1]), .DI(programcounter_1_out_5),
    .DO2(programcounter_1_out_5), .DO1(aregister_1_do1));
  AlgorithmicLogicUnit algorithmiclogicunit_1 (
    .EU(ALU_CABLE[1]), .SU(ALU_CABLE[0]), .AIN(aregister_1_do1), .BIN(bregister_1_out_4),
    .SO(programcounter_1_out_5));
  BRegister bregister_1 (.CLK(AR_CABLE[2]), .nLB(BR_CABLE[0]), .DW(programcounter_1_out_5), .out_4(bregister_1_out_4));
  OutputRegister outputregister_1 (
    .CLK(AR_CABLE[2]), .nLO(nLO), .DW(programcounter_1_out_5), .out_4(outputregister_1_out_4));
  // Probe on aregister_1_do1
  // Probe on bregister_1_out_4
  // Probe on outputregister_1_out_4
  // Digital_Oscilloscope #(.nState(7)) digital_oscilloscope_1: pin names not known; wires that end beside it: AR_CABLE[2], T1, T2, T3, T4, T5, T6, EP, MAR_CABLE[0], CP, nCE

  // Other names for the same wires on the sheet: SU = ALU_CABLE[0]; EU = ALU_CABLE[1]; nLA = AR_CABLE[0];
  //   EA = AR_CABLE[1]; nLB = BR_CABLE[0]; nLI = IR_CABLE[0]; nEI = IR_CABLE[3]; nLM = MAR_CABLE[0];
  //   OR_CABLE[1:0] = {AR_CABLE[2], nLO}; PC_CABLE[3:0] = {EP, nCLK, CS_CABLE[0], CP}; nCLR = CS_CABLE[0];
  //   PIO_CABLE[17:0] = {MAR_CABLE[4:1], PD, MAR_CABLE[6], nW, AR_CABLE[2], nCLK, CLR, CS_CABLE[0]};
  //   IR_CABLE[2:1] = {AR_CABLE[2], CLR}; BR_CABLE[1] = AR_CABLE[2]; CLK = AR_CABLE[2]; CS_CABLE[1] = AR_CABLE[2];
  //   MAR_CABLE[5] = AR_CABLE[2]; RAM_CABLE[9:0] = {PD, nW, nCE}; nPS = MAR_CABLE[6]; PA[3:0] = MAR_CABLE[4:1];
  //   T_STATES[5:0] = {T6, T5, T4, T3, T2, T1}

  // Notes on the sheet:
  //   12⇓ 
  //   4⇓ 
  //   4⇓ 
  //   +---------------------------------------------+
  //   |                             SAP-1 Computer                           |
  //   +---------------------------------------------+
  //   4⇒
  //   ⇐4
  //   8⇒
  //   ⇐8
  //   4⇒
  //   +---------------------------------------------+
  //   |                           Cable Management                         |
  //   +---------------------------------------------+
  //   8⇒
  //   ⇐8
  //   8⇒
  //   8⇒
  //   8⇓ 
  //   8⇑
  //   8⇓ 
endmodule

module ProgramCounter (
  input  CP,
  input  nCLK,
  input  nCLR,
  input  EP,
  output [7:0] out_5
);

  wire and_1_out, j_k_ff_1_q, j_k_ff_2_q, j_k_ff_3_q, j_k_ff_4_q, not_1_out;

  and and_1 (and_1_out, CP, ~nCLK);  // AND_Gate
  J_K_Flip_Flop #(.trigger("falling")) j_k_ff_1 (
    .J(1'b1), .K(1'b1), .clk(and_1_out), .Q(j_k_ff_1_q), .reset(not_1_out));  // open: Qn, preset
  not not_1 (not_1_out, nCLR);
  assign out_5[0] = EP ? j_k_ff_1_q : 1'bz;  // Controlled_Buffer controlled_buffer_1
  J_K_Flip_Flop #(.trigger("falling")) j_k_ff_2 (
    .J(1'b1), .K(1'b1), .clk(j_k_ff_1_q), .Q(j_k_ff_2_q), .reset(not_1_out));  // open: Qn, preset
  J_K_Flip_Flop #(.trigger("falling")) j_k_ff_3 (
    .J(1'b1), .K(1'b1), .clk(j_k_ff_2_q), .Q(j_k_ff_3_q), .reset(not_1_out));  // open: Qn, preset
  assign out_5[1] = EP ? j_k_ff_2_q : 1'bz;  // Controlled_Buffer controlled_buffer_2
  assign out_5[2] = EP ? j_k_ff_3_q : 1'bz;  // Controlled_Buffer controlled_buffer_3
  J_K_Flip_Flop #(.trigger("falling")) j_k_ff_4 (
    .J(1'b1), .K(1'b1), .clk(j_k_ff_3_q), .Q(j_k_ff_4_q), .reset(not_1_out));  // open: Qn, preset
  assign out_5[3] = EP ? j_k_ff_4_q : 1'bz;  // Controlled_Buffer controlled_buffer_4
endmodule

module MemoryAddressRegister (
  input  [7:0] DI,
  input  CLK,
  input  nLM,
  input  [3:0] PA,
  input  nPS,
  output [3:0] DO
);

  wire and_1_out, not_1_out, Q0, Q1, Q2, Q3;

  not not_1 (not_1_out, nLM);
  and and_1 (and_1_out, CLK, not_1_out);
  Multiplexer #(.disabled("Z"), .width(4)) multiplexer_1 (.in0(PA), .in1({Q3, Q2, Q1, Q0}), .out(DO), .sel(nPS));
  D_Flip_Flop d_ff_1 (.D(DI[0]), .clk(and_1_out), .Q(Q0));  // open: Qn, preset, reset
  D_Flip_Flop d_ff_2 (.D(DI[1]), .clk(and_1_out), .Q(Q1));  // open: Qn, preset, reset
  D_Flip_Flop d_ff_3 (.D(DI[2]), .clk(and_1_out), .Q(Q2));  // open: Qn, preset, reset
  D_Flip_Flop d_ff_4 (.D(DI[3]), .clk(and_1_out), .Q(Q3));  // open: Qn, preset, reset

  // Notes on the sheet:
  //   nPS: pull=down, initial=0x1
  //   W BUS Addr
  //   Program Addr
  //   Program/Bus
endmodule

module ReadAccessMemory (
  input  nCE,
  input  nW,
  input  [7:0] DI,
  input  [3:0] ADDR,
  output [7:0] DO
);

  wire nAE0, nAE1, nAE2, nAE3, nAE4, nAE5, nAE6, nAE7, nAE8, nAE9, nAE10, nAE11, nAE12, nAE13, nAE14, nAE15,
       not_2_out, not_3_out, not_4_out, not_5_out, not_6_out, not_7_out, not_8_out, not_9_out, not_10_out,
       not_11_out, not_12_out, not_13_out, not_14_out, nWE, OBE;
  wire [7:0] b0_do;

  not not_1 (OBE, nCE);
  not not_2 (not_2_out, nW);
  nand nand_1 (nWE, OBE, not_2_out);
  not not_3 (not_3_out, ADDR[3]);
  not not_4 (not_4_out, ADDR[2]);
  not not_5 (not_5_out, ADDR[1]);
  not not_6 (not_6_out, ADDR[2]);
  not not_7 (not_7_out, ADDR[1]);
  not not_8 (not_8_out, ADDR[0]);
  not not_9 (not_9_out, ADDR[0]);
  nand nand_2 (nAE0, not_8_out, not_5_out, not_4_out, not_3_out);
  nand nand_3 (nAE1, ADDR[0], not_5_out, not_4_out, not_3_out);
  nand nand_4 (nAE2, not_8_out, ADDR[1], not_4_out, not_3_out);
  nand nand_5 (nAE3, ADDR[0], ADDR[1], not_4_out, not_3_out);
  nand nand_6 (nAE8, not_9_out, not_7_out, not_6_out, ADDR[3]);
  nand nand_7 (nAE9, ADDR[0], not_7_out, not_6_out, ADDR[3]);
  nand nand_8 (nAE10, not_9_out, ADDR[1], not_6_out, ADDR[3]);
  nand nand_9 (nAE11, ADDR[0], ADDR[1], not_6_out, ADDR[3]);
  not not_10 (not_10_out, ADDR[3]);
  not not_11 (not_11_out, ADDR[1]);
  not not_12 (not_12_out, ADDR[0]);
  not not_13 (not_13_out, ADDR[1]);
  not not_14 (not_14_out, ADDR[0]);
  nand nand_10 (nAE4, not_12_out, not_11_out, ADDR[2], not_10_out);
  nand nand_11 (nAE5, ADDR[0], not_11_out, ADDR[2], not_10_out);
  nand nand_12 (nAE6, not_12_out, ADDR[1], ADDR[2], not_10_out);
  nand nand_13 (nAE7, ADDR[0], ADDR[1], ADDR[2], not_10_out);
  nand nand_14 (nAE12, not_14_out, not_13_out, ADDR[2], ADDR[3]);
  nand nand_15 (nAE13, ADDR[0], not_13_out, ADDR[2], ADDR[3]);
  nand nand_16 (nAE14, not_14_out, ADDR[1], ADDR[2], ADDR[3]);
  nand nand_17 (nAE15, ADDR[0], ADDR[1], ADDR[2], ADDR[3]);
  MemoryWord b0 (.nAE(nAE0), .nWE(nWE), .DI(DI), .DO(b0_do));
  MemoryWord b4 (.nAE(nAE4), .nWE(nWE), .DI(DI), .DO(b0_do));
  MemoryWord b8 (.nAE(nAE8), .nWE(nWE), .DI(DI), .DO(b0_do));
  MemoryWord b12 (.nAE(nAE12), .nWE(nWE), .DI(DI), .DO(b0_do));
  MemoryWord b1 (.nAE(nAE1), .nWE(nWE), .DI(DI), .DO(b0_do));
  MemoryWord b5 (.nAE(nAE5), .nWE(nWE), .DI(DI), .DO(b0_do));
  MemoryWord b9 (.nAE(nAE9), .nWE(nWE), .DI(DI), .DO(b0_do));
  MemoryWord b13 (.nAE(nAE13), .nWE(nWE), .DI(DI), .DO(b0_do));
  MemoryWord b2 (.nAE(nAE2), .nWE(nWE), .DI(DI), .DO(b0_do));
  MemoryWord b6 (.nAE(nAE6), .nWE(nWE), .DI(DI), .DO(b0_do));
  MemoryWord b20 (.nAE(nAE10), .nWE(nWE), .DI(DI), .DO(b0_do));
  MemoryWord b14 (.nAE(nAE14), .nWE(nWE), .DI(DI), .DO(b0_do));
  MemoryWord b3 (.nAE(nAE3), .nWE(nWE), .DI(DI), .DO(b0_do));
  MemoryWord b7 (.nAE(nAE7), .nWE(nWE), .DI(DI), .DO(b0_do));
  MemoryWord b11 (.nAE(nAE11), .nWE(nWE), .DI(DI), .DO(b0_do));
  MemoryWord b15 (.nAE(nAE15), .nWE(nWE), .DI(DI), .DO(b0_do));
  assign DO = OBE ? b0_do : 8'bz;  // Controlled_Buffer controlled_buffer_1

  // Notes on the sheet:
  //   ---- Write/Output Buffer Enable ----
  //   0-3
  //   8-11
  //   -------- Address Enable --------
  //   4-7
  //   12-15
  //   -------- 16 Byte RAM --------
endmodule

module InstructionRegister (
  input  [7:0] DW,
  input  CLK,
  input  CLR,
  input  nLI,
  input  nEI,
  output [3:0] HN0,
  output [7:0] LNO
);

  wire and_1_out, and_2_out, d_ff_5_q, d_ff_6_q, d_ff_7_q, d_ff_8_q, nEI_t, nLI_t;

  not not_1 (nLI_t, nLI);
  not not_2 (nEI_t, nEI);
  and and_1 (and_1_out, CLK, nLI_t);
  D_Flip_Flop d_ff_1 (.D(DW[4]), .clk(and_1_out), .Q(HN0[0]), .reset(CLR));  // open: Qn, preset
  D_Flip_Flop d_ff_2 (.D(DW[5]), .clk(and_1_out), .Q(HN0[1]), .reset(CLR));  // open: Qn, preset
  D_Flip_Flop d_ff_3 (.D(DW[6]), .clk(and_1_out), .Q(HN0[2]), .reset(CLR));  // open: Qn, preset
  D_Flip_Flop d_ff_4 (.D(DW[7]), .clk(and_1_out), .Q(HN0[3]), .reset(CLR));  // open: Qn, preset
  and and_2 (and_2_out, CLK, nLI_t);
  D_Flip_Flop d_ff_5 (.D(DW[0]), .clk(and_2_out), .Q(d_ff_5_q), .reset(CLR));  // open: Qn, preset
  D_Flip_Flop d_ff_6 (.D(DW[1]), .clk(and_2_out), .Q(d_ff_6_q), .reset(CLR));  // open: Qn, preset
  D_Flip_Flop d_ff_7 (.D(DW[2]), .clk(and_2_out), .Q(d_ff_7_q), .reset(CLR));  // open: Qn, preset
  D_Flip_Flop d_ff_8 (.D(DW[3]), .clk(and_2_out), .Q(d_ff_8_q), .reset(CLR));  // open: Qn, preset
  assign LNO[0] = nEI_t ? d_ff_5_q : 1'bz;  // Controlled_Buffer controlled_buffer_1
  assign LNO[1] = nEI_t ? d_ff_6_q : 1'bz;  // Controlled_Buffer controlled_buffer_2
  assign LNO[2] = nEI_t ? d_ff_7_q : 1'bz;  // Controlled_Buffer controlled_buffer_3
  assign LNO[3] = nEI_t ? d_ff_8_q : 1'bz;  // Controlled_Buffer controlled_buffer_4

  // Other names for the same wires on the sheet: LN[3:0] = DW[3:0]; UN[3:0] = DW[7:4]

  // Notes on the sheet:
  //   -------- Upper Nibble --------
  //   ⇒ CS
  //   -------- Lower Nibble --------
  //   ⇒ W BUS
endmodule

module ControllerSequencer (
  input  CLK,
  input  nCLR,
  input  [3:0] A,
  output [5:0] T,
  output nHLT,
  output [11:0] out_6
);

  wire instructiondecoder_1_add, instructiondecoder_1_lda, instructiondecoder_1_oup,
       instructiondecoder_1_sub, nand_1_out, nand_2_out, nand_3_out, nand_4_out, nand_5_out, nand_6_out,
       nand_7_out, nand_8_out, nand_9_out, nand_10_out, nand_11_out, nand_12_out, nand_13_out, nand_14_out,
       nand_15_out, nand_16_out, nand_17_out, nand_18_out, not_1_out, not_3_out, or_1_out, or_2_out,
       or_3_out, or_4_out, or_6_out;

  RingCounter ringcounter_1 (
    .CLK(CLK), .nCLR(nCLR), .T1(out_6[10]), .T2(out_6[11]), .T3(T[2]), .T4(T[3]), .T5(T[4]), .T6(T[5]));
  InstructionDecoder instructiondecoder_1 (
    .I7(A[3]), .I6(A[2]), .I5(A[1]), .I4(A[0]), .LDA(instructiondecoder_1_lda),
    .ADD(instructiondecoder_1_add), .SUB(instructiondecoder_1_sub), .OUP(instructiondecoder_1_oup),
    .nHLT(nHLT));
  not not_1 (not_1_out, out_6[10]);
  nand nand_1 (nand_1_out, instructiondecoder_1_lda, T[3]);
  nand nand_2 (nand_2_out, instructiondecoder_1_add, T[3]);
  or or_1 (or_1_out, ~not_1_out, ~nand_1_out, ~nand_2_out, ~nand_3_out);  // OR_Gate
  not not_2 (out_6[9], or_1_out);
  nand nand_3 (nand_3_out, instructiondecoder_1_sub, T[3]);
  nand nand_4 (nand_4_out, instructiondecoder_1_lda, T[4]);
  not not_3 (not_3_out, T[2]);
  nand nand_5 (nand_5_out, instructiondecoder_1_add, T[4]);
  or or_2 (or_2_out, ~nand_4_out, ~not_3_out, ~nand_5_out, ~nand_6_out);  // OR_Gate
  not not_4 (out_6[8], or_2_out);
  nand nand_6 (nand_6_out, instructiondecoder_1_sub, T[4]);
  nand nand_7 (nand_7_out, instructiondecoder_1_lda, T[3]);
  not not_5 (out_6[7], T[2]);
  nand nand_8 (nand_8_out, instructiondecoder_1_add, T[3]);
  or or_3 (or_3_out, ~nand_7_out, ~nand_8_out, ~nand_9_out);  // OR_Gate
  not not_6 (out_6[6], or_3_out);
  nand nand_9 (nand_9_out, instructiondecoder_1_sub, T[3]);
  nand nand_10 (nand_10_out, instructiondecoder_1_lda, T[4]);
  nand nand_11 (nand_11_out, instructiondecoder_1_add, T[5]);
  or or_4 (or_4_out, ~nand_10_out, ~nand_11_out, ~nand_12_out);  // OR_Gate
  not not_7 (out_6[5], or_4_out);
  nand nand_12 (nand_12_out, instructiondecoder_1_sub, T[5]);
  nand nand_13 (nand_13_out, instructiondecoder_1_oup, T[3]);
  not not_8 (out_6[4], nand_13_out);
  nand nand_14 (nand_14_out, instructiondecoder_1_sub, T[5]);
  nand nand_15 (nand_15_out, instructiondecoder_1_add, T[5]);
  not not_9 (out_6[3], nand_14_out);
  nand nand_16 (nand_16_out, instructiondecoder_1_sub, T[5]);
  or or_5 (out_6[2], ~nand_15_out, ~nand_16_out);  // OR_Gate
  nand nand_17 (nand_17_out, instructiondecoder_1_add, T[4]);
  nand nand_18 (nand_18_out, instructiondecoder_1_sub, T[4]);
  or or_6 (or_6_out, ~nand_17_out, ~nand_18_out);  // OR_Gate
  not not_10 (out_6[1], or_6_out);
  nand nand_19 (out_6[0], instructiondecoder_1_oup, T[3]);

  assign T[1:0] = out_6[11:10];

  // Other names for the same wires on the sheet: nLO = out_6[0]; nLB = out_6[1]; EU = out_6[2]; SU = out_6[3];
  //   EA = out_6[4]; nLA = out_6[5]; nEI = out_6[6]; nLI = out_6[7]; nCE = out_6[8]; nLM = out_6[9]; EP = out_6[10];
  //   CP = out_6[11]

  // Notes on the sheet:
  //   ⇓ 
  //   ---- Op Codes ----
  //   LDA    0000
  //   ADD    0001
  //   SUB     0010
  //   OUT    1110
  //   HLT    1111
  //   -----------------
endmodule

module ARegister (
  input  [7:0] DI,
  input  CLK,
  input  nLA,
  input  EA,
  output [7:0] DO2,
  output [7:0] DO1
);

  wire and_1_out, and_2_out, nLA_t;

  not not_1 (nLA_t, nLA);
  and and_1 (and_1_out, CLK, nLA_t);
  D_Flip_Flop d_ff_1 (.D(DI[4]), .clk(and_1_out), .Q(DO1[4]));  // open: Qn, preset, reset
  D_Flip_Flop d_ff_2 (.D(DI[5]), .clk(and_1_out), .Q(DO1[5]));  // open: Qn, preset, reset
  D_Flip_Flop d_ff_3 (.D(DI[6]), .clk(and_1_out), .Q(DO1[6]));  // open: Qn, preset, reset
  D_Flip_Flop d_ff_4 (.D(DI[7]), .clk(and_1_out), .Q(DO1[7]));  // open: Qn, preset, reset
  assign DO2[4] = EA ? DO1[4] : 1'bz;  // Controlled_Buffer controlled_buffer_1
  assign DO2[5] = EA ? DO1[5] : 1'bz;  // Controlled_Buffer controlled_buffer_2
  assign DO2[6] = EA ? DO1[6] : 1'bz;  // Controlled_Buffer controlled_buffer_3
  assign DO2[7] = EA ? DO1[7] : 1'bz;  // Controlled_Buffer controlled_buffer_4
  and and_2 (and_2_out, CLK, nLA_t);
  D_Flip_Flop d_ff_5 (.D(DI[0]), .clk(and_2_out), .Q(DO1[0]));  // open: Qn, preset, reset
  D_Flip_Flop d_ff_6 (.D(DI[1]), .clk(and_2_out), .Q(DO1[1]));  // open: Qn, preset, reset
  D_Flip_Flop d_ff_7 (.D(DI[2]), .clk(and_2_out), .Q(DO1[2]));  // open: Qn, preset, reset
  D_Flip_Flop d_ff_8 (.D(DI[3]), .clk(and_2_out), .Q(DO1[3]));  // open: Qn, preset, reset
  assign DO2[0] = EA ? DO1[0] : 1'bz;  // Controlled_Buffer controlled_buffer_5
  assign DO2[1] = EA ? DO1[1] : 1'bz;  // Controlled_Buffer controlled_buffer_6
  assign DO2[2] = EA ? DO1[2] : 1'bz;  // Controlled_Buffer controlled_buffer_7
  assign DO2[3] = EA ? DO1[3] : 1'bz;  // Controlled_Buffer controlled_buffer_8

  // Other names for the same wires on the sheet: LNO_ALU[3:0] = DO1[3:0]; UNO_ALU[3:0] = DO1[7:4];
  //   LNO_WBUS[3:0] = DO2[3:0]; UNO_WBUS[3:0] = DO2[7:4]; LN[3:0] = DI[3:0]; UN[3:0] = DI[7:4]

  // Notes on the sheet:
  //   -------- Upper Nibble --------
  //   -------- Lower Nibble --------
  //   ⇒ W BUS
  //   ⇒ ALU
endmodule

module AlgorithmicLogicUnit (
  input  [7:0] AIN,
  input  [7:0] BIN,
  input  SU,
  input  EU,
  output [7:0] SO
);

  wire nibbleadder_2_cout;
  wire [3:0] LSO, USO;

  NibbleAdder nibbleadder_1 (
    .SU(SU), .CIN(nibbleadder_2_cout), .AIN(AIN[7:4]), .BIN(BIN[7:4]), .SOUT(USO));  // open: COUT
  NibbleAdder nibbleadder_2 (.SU(SU), .CIN(SU), .AIN(AIN[3:0]), .BIN(BIN[3:0]), .SOUT(LSO), .COUT(nibbleadder_2_cout));
  assign SO = EU ? {USO, LSO} : 8'bz;  // Controlled_Buffer controlled_buffer_1

  // Other names for the same wires on the sheet: ALN[3:0] = AIN[3:0]; AUN[3:0] = AIN[7:4]; BLN[3:0] = BIN[3:0];
  //   BUN[3:0] = BIN[7:4]

  // Notes on the sheet:
  //   Adds/subtracts the upper nibbles
  //   Adds/subtracts the lower nibbles
endmodule

module BRegister (
  input  [7:0] DW,
  input  CLK,
  input  nLB,
  output [7:0] out_4
);

  wire and_1_out, and_2_out, nLB_t;

  not not_1 (nLB_t, nLB);
  and and_1 (and_1_out, CLK, nLB_t);
  D_Flip_Flop d_ff_1 (.D(DW[4]), .clk(and_1_out), .Q(out_4[4]));  // open: Qn, preset, reset
  D_Flip_Flop d_ff_2 (.D(DW[5]), .clk(and_1_out), .Q(out_4[5]));  // open: Qn, preset, reset
  D_Flip_Flop d_ff_3 (.D(DW[6]), .clk(and_1_out), .Q(out_4[6]));  // open: Qn, preset, reset
  D_Flip_Flop d_ff_4 (.D(DW[7]), .clk(and_1_out), .Q(out_4[7]));  // open: Qn, preset, reset
  and and_2 (and_2_out, CLK, nLB_t);
  D_Flip_Flop d_ff_5 (.D(DW[0]), .clk(and_2_out), .Q(out_4[0]));  // open: Qn, preset, reset
  D_Flip_Flop d_ff_6 (.D(DW[1]), .clk(and_2_out), .Q(out_4[1]));  // open: Qn, preset, reset
  D_Flip_Flop d_ff_7 (.D(DW[2]), .clk(and_2_out), .Q(out_4[2]));  // open: Qn, preset, reset
  D_Flip_Flop d_ff_8 (.D(DW[3]), .clk(and_2_out), .Q(out_4[3]));  // open: Qn, preset, reset

  // Other names for the same wires on the sheet: LN[3:0] = DW[3:0]; LNO[3:0] = out_4[3:0]; UNO[3:0] = out_4[7:4];
  //   UN[3:0] = DW[7:4]
endmodule

module OutputRegister (
  input  [7:0] DW,
  input  CLK,
  input  nLO,
  output [7:0] out_4
);

  wire and_1_out, and_2_out, nLO_t;

  not not_1 (nLO_t, nLO);
  and and_1 (and_1_out, CLK, nLO_t);
  D_Flip_Flop d_ff_1 (.D(DW[4]), .clk(and_1_out), .Q(out_4[4]));  // open: Qn, preset, reset
  D_Flip_Flop d_ff_2 (.D(DW[5]), .clk(and_1_out), .Q(out_4[5]));  // open: Qn, preset, reset
  D_Flip_Flop d_ff_3 (.D(DW[6]), .clk(and_1_out), .Q(out_4[6]));  // open: Qn, preset, reset
  D_Flip_Flop d_ff_4 (.D(DW[7]), .clk(and_1_out), .Q(out_4[7]));  // open: Qn, preset, reset
  D_Flip_Flop d_ff_5 (.D(DW[0]), .clk(and_2_out), .Q(out_4[0]));  // open: Qn, preset, reset
  D_Flip_Flop d_ff_6 (.D(DW[1]), .clk(and_2_out), .Q(out_4[1]));  // open: Qn, preset, reset
  D_Flip_Flop d_ff_7 (.D(DW[2]), .clk(and_2_out), .Q(out_4[2]));  // open: Qn, preset, reset
  D_Flip_Flop d_ff_8 (.D(DW[3]), .clk(and_2_out), .Q(out_4[3]));  // open: Qn, preset, reset
  and and_2 (and_2_out, CLK, nLO_t);

  // Other names for the same wires on the sheet: LN[3:0] = DW[3:0]; LNO[3:0] = out_4[3:0]; UNO[3:0] = out_4[7:4];
  //   UN[3:0] = DW[7:4]

  // Notes on the sheet:
  //   DW: pull=down
endmodule

// ID
module InstructionDecoder (
  input  I7,
  input  I6,
  input  I5,
  input  I4,
  output LDA,
  output ADD,
  output SUB,
  output OUP,
  output nHLT
);

  wire not_1_out, not_2_out, not_3_out, not_4_out;

  not not_1 (not_1_out, I7);
  not not_2 (not_2_out, I6);
  not not_3 (not_3_out, I5);
  not not_4 (not_4_out, I4);
  and and_1 (LDA, not_1_out, not_2_out, not_3_out, not_4_out);
  and and_2 (ADD, not_1_out, not_2_out, not_3_out, I4);
  and and_3 (SUB, not_1_out, not_2_out, I5, not_4_out);
  and and_4 (OUP, I7, I6, I5, not_4_out);
  nand nand_1 (nHLT, I7, I6, I5, I4);
endmodule

// RC
module RingCounter (
  input  CLK,
  input  nCLR,
  output T1,
  output T2,
  output T3,
  output T4,
  output T5,
  output T6
);

  wire j_k_ff_1_q, j_k_ff_2_qn, j_k_ff_3_qn, j_k_ff_4_qn, j_k_ff_5_qn, j_k_ff_6_qn, not_1_out;

  J_K_Flip_Flop #(.trigger("falling")) j_k_ff_1 (
    .J(j_k_ff_6_qn), .K(T6), .clk(CLK), .Q(j_k_ff_1_q), .Qn(T1), .reset(not_1_out));  // open: preset
  not not_1 (not_1_out, nCLR);
  J_K_Flip_Flop #(.trigger("falling")) j_k_ff_2 (
    .J(T1), .K(j_k_ff_1_q), .clk(CLK), .Q(T2), .Qn(j_k_ff_2_qn), .reset(not_1_out));  // open: preset
  J_K_Flip_Flop #(.trigger("falling")) j_k_ff_3 (
    .J(T2), .K(j_k_ff_2_qn), .clk(CLK), .Q(T3), .Qn(j_k_ff_3_qn), .reset(not_1_out));  // open: preset
  J_K_Flip_Flop #(.trigger("falling")) j_k_ff_4 (
    .J(T3), .K(j_k_ff_3_qn), .clk(CLK), .Q(T4), .Qn(j_k_ff_4_qn), .reset(not_1_out));  // open: preset
  J_K_Flip_Flop #(.trigger("falling")) j_k_ff_5 (
    .J(T4), .K(j_k_ff_4_qn), .clk(CLK), .Q(T5), .Qn(j_k_ff_5_qn), .reset(not_1_out));  // open: preset
  J_K_Flip_Flop #(.trigger("falling")) j_k_ff_6 (
    .J(T5), .K(j_k_ff_5_qn), .clk(CLK), .Q(T6), .Qn(j_k_ff_6_qn), .reset(not_1_out));  // open: preset
endmodule

module MemoryWord (
  input  [7:0] DI,
  input  nAE,
  input  nWE,
  output [7:0] DO
);

  wire and_1_out, and_2_out, d_ff_1_q, d_ff_2_q, d_ff_3_q, d_ff_4_q, d_ff_5_q, d_ff_6_q, d_ff_7_q, d_ff_8_q,
       not_1_out, not_2_out;

  not not_1 (not_1_out, nAE);
  not not_2 (not_2_out, nWE);
  and and_1 (and_1_out, not_1_out, not_2_out);
  and and_2 (and_2_out, not_1_out, nWE);
  D_Flip_Flop #(.trigger("falling")) d_ff_1 (.D(DI[0]), .clk(and_1_out), .Q(d_ff_1_q));  // open: Qn, preset, reset
  D_Flip_Flop #(.trigger("falling")) d_ff_2 (.D(DI[1]), .clk(and_1_out), .Q(d_ff_2_q));  // open: Qn, preset, reset
  D_Flip_Flop #(.trigger("falling")) d_ff_3 (.D(DI[2]), .clk(and_1_out), .Q(d_ff_3_q));  // open: Qn, preset, reset
  D_Flip_Flop #(.trigger("falling")) d_ff_4 (.D(DI[3]), .clk(and_1_out), .Q(d_ff_4_q));  // open: Qn, preset, reset
  D_Flip_Flop #(.trigger("falling")) d_ff_5 (.D(DI[4]), .clk(and_1_out), .Q(d_ff_5_q));  // open: Qn, preset, reset
  D_Flip_Flop #(.trigger("falling")) d_ff_6 (.D(DI[5]), .clk(and_1_out), .Q(d_ff_6_q));  // open: Qn, preset, reset
  D_Flip_Flop #(.trigger("falling")) d_ff_7 (.D(DI[6]), .clk(and_1_out), .Q(d_ff_7_q));  // open: Qn, preset, reset
  D_Flip_Flop #(.trigger("falling")) d_ff_8 (.D(DI[7]), .clk(and_1_out), .Q(d_ff_8_q));  // open: Qn, preset, reset
  assign DO[0] = and_2_out ? d_ff_1_q : 1'bz;  // Controlled_Buffer controlled_buffer_1
  assign DO[1] = and_2_out ? d_ff_2_q : 1'bz;  // Controlled_Buffer controlled_buffer_2
  assign DO[2] = and_2_out ? d_ff_3_q : 1'bz;  // Controlled_Buffer controlled_buffer_3
  assign DO[3] = and_2_out ? d_ff_4_q : 1'bz;  // Controlled_Buffer controlled_buffer_4
  assign DO[4] = and_2_out ? d_ff_5_q : 1'bz;  // Controlled_Buffer controlled_buffer_5
  assign DO[5] = and_2_out ? d_ff_6_q : 1'bz;  // Controlled_Buffer controlled_buffer_6
  assign DO[6] = and_2_out ? d_ff_7_q : 1'bz;  // Controlled_Buffer controlled_buffer_7
  assign DO[7] = and_2_out ? d_ff_8_q : 1'bz;  // Controlled_Buffer controlled_buffer_8

  // Notes on the sheet:
  //   Data (Lower Nibble)
  //   OpCode (Higher Nibble)
endmodule

module WBus (
  input  [7:0] I,
  output [7:0] O
);


  assign O = I;
endmodule

module ControlPanel (
  input  S2,
  input  CS,
  input  [3:0] S1,
  input  [7:0] S3,
  input  S4,
  input  nHLT,
  input  SS,
  input  MAN,
  output nCLR,
  output Run,
  output Program,
  output nPS,
  output CLR,
  output [3:0] PA,
  output [7:0] PD,
  output nW,
  output CLK,
  output nCLK,
  output MANUAL,
  output AUTO
);

  wire clock_1_out, j_k_ff_1_q, nand_1_out, nand_2_out, nand_5_out, nand_6_out, not_2_out, not_3_out,
       not_4_out, not_5_out, not_6_out, or_3_out;

  not not_1 (Program, S2);
  J_K_Flip_Flop j_k_ff_1 (
    .J(nHLT), .K(nHLT), .clk(clock_1_out), .Q(j_k_ff_1_q), .reset(not_2_out));  // open: Qn, preset
  Clock clock_1 (.out(clock_1_out));
  not not_2 (not_2_out, nCLR);
  not not_3 (not_3_out, CS);
  not not_4 (not_4_out, SS);
  nand nand_1 (nand_1_out, not_4_out, nand_2_out);
  nand nand_2 (nand_2_out, nand_1_out, SS);
  not not_5 (not_5_out, MAN);
  nand nand_3 (MANUAL, not_5_out, AUTO);
  nand nand_4 (AUTO, MANUAL, MAN);
  or or_1 (nCLR, ~CS, ~CLR);  // OR_Gate
  or or_2 (CLR, ~nCLR, ~not_3_out);  // OR_Gate
  nand nand_5 (nand_5_out, nHLT, nand_2_out, MANUAL);
  nand nand_6 (nand_6_out, AUTO, j_k_ff_1_q);
  or or_3 (or_3_out, ~nand_5_out, ~nand_6_out);  // OR_Gate
  not not_6 (not_6_out, or_3_out);
  not not_7 (nCLK, or_3_out);
  not not_8 (CLK, not_6_out);

  assign nPS = S2;
  assign nW = S4;
  assign PA = S1;
  assign PD = S3;
  assign Run = S2;

  // Notes on the sheet:
  //   S2: pull=down
  //   Clock
  //   Clear-start Debouncer
  //   Single-step Debouncer
  //   Manual-auto Debouncer
  //   Clock Buffers
endmodule

module FullAdder (
  input  A,
  input  B,
  input  CIN,
  output SUM,
  output COUT
);

  wire and_1_out, and_2_out, xor_1_out;

  xor xor_1 (xor_1_out, A, B);
  xor xor_2 (SUM, xor_1_out, CIN);
  and and_1 (and_1_out, CIN, xor_1_out);
  and and_2 (and_2_out, A, B);
  or or_1 (COUT, and_1_out, and_2_out);
endmodule

module NibbleAdder (
  input  [3:0] AIN,
  input  [3:0] BIN,
  input  SU,
  input  CIN,
  output [3:0] SOUT,
  output COUT
);

  wire B0, B1, B2, B3, fulladder_1_cout, fulladder_2_cout, fulladder_3_cout;

  xor xor_1 (B0, BIN[0], SU);
  xor xor_2 (B1, BIN[1], SU);
  xor xor_3 (B2, BIN[2], SU);
  xor xor_4 (B3, BIN[3], SU);
  FullAdder fulladder_1 (.A(AIN[0]), .B(B0), .CIN(CIN), .SUM(SOUT[0]), .COUT(fulladder_1_cout));
  FullAdder fulladder_2 (.A(AIN[1]), .B(B1), .CIN(fulladder_1_cout), .SUM(SOUT[1]), .COUT(fulladder_2_cout));
  FullAdder fulladder_3 (.A(AIN[2]), .B(B2), .CIN(fulladder_2_cout), .SUM(SOUT[2]), .COUT(fulladder_3_cout));
  FullAdder fulladder_4 (.A(AIN[3]), .B(B3), .CIN(fulladder_3_cout), .SUM(SOUT[3]), .COUT(COUT));

  // Other names for the same wires on the sheet: A0 = AIN[0]; A1 = AIN[1]; A2 = AIN[2]; A3 = AIN[3]; S0 = SOUT[0];
  //   S1 = SOUT[1]; S2 = SOUT[2]; S3 = SOUT[3]
endmodule
